# Fritzing sketch LEDsBrightness (saved by Fritzing 0.9.3b)
breadboards: 1

parts:
  LED3 = RGB LED (com. cathode, rgb) [package="5 mm [THT]"]
  元件2 = SwiftIO

nets:
  N1: LED3.red_anode, 元件2.P10/D10/PWM2B
  N2: LED3.common_cathode, 元件2.GND
  N3: LED3.green_anode, 元件2.P4/D4/PWM0A
  N4: LED3.blue_anode, 元件2.P9/D9/SPI0_CS

custom parts:
  SwiftIO: SwiftIO offers a full Swift compiler and framework environment that runs on the microcontroller. The SwiftIO board is a compact electronic circuit board that runs Swift on the bare metal, giving you a system that can be used to control all kinds of electronic projects.
