# Fritzing sketch PWMMelody (saved by Fritzing 0.9.3b)

parts:
  元件1 = SwiftIO
  J1 = Piezo Speaker

nets:
  N1: 元件1.R02, J1.pin1
  N2: 元件1.R32, J1.pin2

custom parts:
  SwiftIO: SwiftIO offers a full Swift compiler and framework environment that runs on the microcontroller. The SwiftIO board is a compact electronic circuit board that runs Swift on the bare metal, giving you a system that can be used to control all kinds of electronic projects.
